# Fritzing sketch levitation (saved by Fritzing 0.8.3b)

parts:
  Arduino = Arduino Uno (Rev3)
  Lev_Fan = DC Motor
  D1 = Rectifier Diode [part_number=1N4001 package="300 mil [THT]"]
  V1 = DC Power [voltage=12V]
  Q1 = Basic FET N-Channel [package="DPak [SMD]"]
  R2 = Resistor [tolerance=±5% resistance=1k package=THT]
  S1 = Square Pushbutton
  R3 = Resistor [tolerance=±5% resistance=10k package=THT]

nets:
  GND: Arduino.GND, V1.V-, Q1.source, R3.Pin_1
  N1: Arduino.D3_PWM, R2.Pin_0
  N2: Lev_Fan.pin_1, D1.cathode, S1.leg0
  N3: Lev_Fan.pin_2, D1.anode, Q1.drain
  N4: V1.V+, S1.leg1
  N5: Q1.Gate, R2.Pin_1, R3.Pin_0
