# Fritzing sketch payload (saved by Fritzing 0.8.3b)

parts:
  Arduino = Arduino Uno (Rev3)
  J2 = Basic Servo
  J1 = Basic Servo
  S1 = Square Pushbutton
  V1 = DC Power [voltage=12V]
  5V = Voltage Regulator - 5V [package="DPak [SMD]"]
  M1 = DC Motor
  Q2 = Basic FET N-Channel [package="DPak [SMD]"]
  R7 = Resistor [tolerance=±5% resistance=1k package=THT]
  R8 = Resistor [tolerance=±5% resistance=10k package=THT]
  D4 = Rectifier Diode [part_number=1N4001 package="300 mil [THT]"]

nets:
  N1: Arduino.ICSP_MISO, Arduino.D12/MISO, J2.pulse
  N2: Arduino.ICSP_SCK, J1.pulse
  N3: Arduino.ICSP_MOSI, Arduino.D11_PWM/MOSI, R7.Pin_0
  GND: Arduino.GND, Q2.source, R8.Pin_0
  GND_2: J2.gnd, J1.gnd, V1.V-, 5V.GND
  VCC: J2.vcc, J1.vcc, 5V.output_voltage
  N4: S1.leg0, 5V.input_voltage, M1.pin_2, D4.cathode
  N5: S1.leg1, V1.V+
  N6: M1.pin_1, Q2.drain, D4.anode
  N7: Q2.Gate, R7.Pin_1, R8.Pin_1
