# Fritzing sketch propulsion (saved by Fritzing 0.8.3b)

parts:
  Arduino_Uno = Arduino Uno (Rev3)
  M1 = DC Motor
  M2 = DC Motor
  Q1 = Basic FET N-Channel [package="DPak [SMD]"]
  Q2 = Basic FET N-Channel [package="DPak [SMD]"]
  D3 = Rectifier Diode [part_number=1N4001 package="300 mil [THT]"]
  D4 = Rectifier Diode [part_number=1N4001 package="300 mil [THT]"]
  V1 = DC Power [voltage=12V]
  S1 = Square Pushbutton
  M3 = DC Motor
  M4 = DC Motor
  M5 = DC Motor
  Q3 = Basic FET N-Channel [package="DPak [SMD]"]
  D5 = Rectifier Diode [part_number=1N4001 package="300 mil [THT]"]
  D6 = Rectifier Diode [part_number=1N4001 package="300 mil [THT]"]
  D7 = Rectifier Diode [part_number=1N4001 package="300 mil [THT]"]
  R3 = Resistor [tolerance=±5% resistance=10k package=THT]
  R4 = Resistor [tolerance=±5% resistance=10k package=THT]
  R5 = Resistor [tolerance=±5% resistance=10k package=THT]
  R6 = Resistor [tolerance=±5% resistance=1k package=THT]
  R7 = Resistor [tolerance=±5% resistance=1k package=THT]
  R8 = Resistor [tolerance=±5% resistance=1k package=THT]

nets:
  GND: Arduino_Uno.GND, Q1.source, Q2.source, V1.V-, Q3.source, R3.Pin_1, R4.Pin_1, R5.Pin_1
  N1: Arduino_Uno.D9_PWM, R7.Pin_1
  N2: Arduino_Uno.D10_PWM/SS, R6.Pin_1
  N3: Arduino_Uno.D5_PWM, R8.Pin_1
  N4: M1.pin_1, M2.pin_1, D3.cathode, D4.cathode, S1.leg0, M3.pin_1, M4.pin_1, M5.pin_1, D5.cathode, D6.cathode, D7.cathode
  N5: M1.pin_2, Q1.drain, D3.anode, M3.pin_2, D5.anode
  N6: M2.pin_2, Q2.drain, D4.anode
  N7: Q1.Gate, R5.Pin_0, R6.Pin_0
  N8: Q2.Gate, R4.Pin_0, R7.Pin_0
  N9: V1.V+, S1.leg1
  N10: M4.pin_2, M5.pin_2, Q3.drain, D6.anode, D7.anode
  N11: Q3.Gate, R3.Pin_0, R8.Pin_0
