# Fritzing sketch sensors (saved by Fritzing 0.8.3b)

parts:
  Arduino_Uno = Arduino Uno (Rev3)
  V1 = DC Power [voltage=12V]
  R3 = Photocell (LDR) [package=THT]
  R4 = Photocell (LDR) [package=THT]
  R5 = Resistor [tolerance=±5% resistance=10k package=THT]
  R6 = Resistor [tolerance=±5% resistance=10k package=THT]
  R7 = Photocell (LDR) [package=THT]
  R8 = Resistor [tolerance=±5% resistance=10k package=THT]
  LED1 = LED - 5mm [color="Red (633nm)" package="5 mm [THT]"]
  LED2 = LED - 5mm [color="Red (633nm)" package="5 mm [THT]"]
  LED3 = LED - 5mm [color="Red (633nm)" package="5 mm [THT]"]
  R9 = Resistor [tolerance=±5% resistance=200 package=THT]
  R10 = Resistor [tolerance=±5% resistance=200 package=THT]
  R11 = Resistor [tolerance=±5% resistance=200 package=THT]
  J3 = Infrared Proximity Sensor
  RF_Rec1 = RF-LINK_RX [package=rf-link_rx]
  S2 = Square Pushbutton
  5V = Voltage Regulator - 5V [package="DPak [SMD]"]

nets:
  N1: Arduino_Uno.A0, R3.pin_1, R5.Pin_1
  N2: Arduino_Uno.A1, R7.pin_1, R8.Pin_1
  N3: Arduino_Uno.A2, R4.pin_1, R6.Pin_1
  5V: Arduino_Uno.5V, R3.pin_0, R4.pin_0, R7.pin_0, J3.Vcc, RF_Rec1.+5V, 5V.output_voltage
  GND: Arduino_Uno.GND, V1.V-, R5.Pin_0, R6.Pin_0, R8.Pin_0, LED1.cathode, LED2.cathode, LED3.cathode, J3.GND, RF_Rec1.GND, 5V.GND
  N4: Arduino_Uno.D4, J3.Vout
  N5: Arduino_Uno.D7, RF_Rec1.DATA
  N6: V1.V+, S2.leg1
  N7: LED1.anode, R9.Pin_0
  N8: LED2.anode, R10.Pin_0
  N9: LED3.anode, R11.Pin_0
  N10: R9.Pin_1, R10.Pin_1, R11.Pin_1
  N11: S2.leg0, 5V.input_voltage
